# Fritzing sketch SchemaProjetEric (saved by Fritzing 0.9.0b)
circuit board: 2.81821cm x 4.9989cm
breadboards: 1

parts:
  Composant1 = Arduino Mega 2560 (Rev3)
  R2 = Resistor [package="2010 [SMD]"]
  R3 = Resistor [package="2010 [SMD]"]
  R4 = Resistor [package="2010 [SMD]"]
  R5 = Resistor [package="2010 [SMD]"]
  R8 = Resistor [tolerance=±5% resistance=1k package=THT]
  R9 = Resistor [tolerance=±5% resistance=1k package=THT]
  LED1 = LED - 5mm [color="Red (633nm)" package="5 mm [THT]"]
  LED2 = LED - 5mm [color="Red (633nm)" package="5 mm [THT]"]
  S1 = Pushbutton [package="[THT]"]
  S2 = Pushbutton [package="[THT]"]
  S4 = Pushbutton [package="[THT]"]
  C1 = Tantalum Capacitor [capacitance=1nF package="200 mil [THT, tantalum]"]
  C2 = Tantalum Capacitor [capacitance=1nF package="200 mil [THT, tantalum]"]
  C3 = Tantalum Capacitor [capacitance=1nF package="200 mil [THT, tantalum]"]
  C4 = Tantalum Capacitor [capacitance=1nF package="200 mil [THT, tantalum]"]
  U1 = G3VM-61E1 [package=g3vm-61e1]
  LED3 = LED - 5mm [color="Red (633nm)" package="5 mm [THT]"]
  VCC1 = 4 x AAA Battery Mount
  S3 = Pushbutton [package="[THT]"]

nets:
  N1: Composant1.5V, R8.Pin_1, R9.Pin_1, S1.Pin_3, S2.Pin_3, S4.Pin_3, U1.P$5, S3.Pin_3
  N2: Composant1.D22, R5.Pin_0
  N3: Composant1.D23, R3.Pin_1
  N4: Composant1.D24, R2.Pin_1
  N5: Composant1.D25, R4.Pin_1
  N6: Composant1.D34, LED2.cathode
  N7: Composant1.D35, LED1.cathode
  N8: Composant1.D36, C2.-
  N9: Composant1.D37, C1.-
  N10: Composant1.D38, C3.-
  N11: Composant1.D39, C4.-
  N12: Composant1.D40, U1.P$4
  N13: Composant1.GND, U1.P$6
  N14: R9.Pin_0, LED1.anode
  N15: U1.P$1, LED3.anode
  N16: U1.P$2, VCC1.+
  N17: LED3.cathode, VCC1.-

notes:
  | | | || |
  8. 8. 8. 8.
  | | | || |
  1 nf
  220 V
  lampe Eric
  | | |
  - + S
  srd-05-vdc-sl-c
  * ** ***
  | | |
  * NO
  220V dirigé vers le composant
  ** COM
  220V venant de la sourse (prise)
  *** NC
  X (rien)
